// Logisim project ALU.circ as structural Verilog: 1 circuit, main circuit ALU
module ALU (
  input  [7:0] A,
  input  [7:0] B,
  input  [1:0] Funct,
  input  [1:0] ALUOp,
  output ZERO,
  output [7:0] ALUSaida,
  output Overflow
);

  wire and_1_out, and_2_out, and_3_out, or_1_out, xnor_1_out, xnor_2_out, xnor_3_out, xnor_4_out, xnor_5_out,
       xnor_6_out, xnor_7_out, xnor_8_out;
  wire [1:0] multiplexer_2_out, multiplexer_3_out;
  wire [7:0] adder_1_out, adder_2_out, and_4_out, multiplexer_1_out, not_1_out, or_2_out;

  assign not_1_out = ~B;  // NOT_Gate not_1, 8 bits wide
  Multiplexer #(.width(8)) multiplexer_1 (.in0(B), .in1(adder_1_out), .out(multiplexer_1_out), .sel(or_1_out));
  Adder adder_1 (.a(not_1_out), .b(8'h1), .out(adder_1_out));  // open: cin, cout
  or or_1 (or_1_out, and_1_out, and_2_out);
  and and_1 (and_1_out, Funct[0], Funct[1], ALUOp[1]);
  and and_2 (and_2_out, ~ALUOp[1], ALUOp[0]);  // AND_Gate
  Adder adder_2 (.a(A), .b(multiplexer_1_out), .out(adder_2_out), .cout(Overflow));  // open: cin
  Multiplexer #(.width(2)) multiplexer_2 (.in0(2'b10), .in1(2'b11), .out(multiplexer_2_out), .sel(and_3_out));
  and and_3 (and_3_out, ~ALUOp[0], ~ALUOp[1]);  // AND_Gate
  assign and_4_out = A & multiplexer_1_out;  // AND_Gate and_4, 8 bits wide
  assign or_2_out = A | multiplexer_1_out;  // OR_Gate or_2, 8 bits wide
  Multiplexer #(.width(2)) multiplexer_3 (
    .in0(multiplexer_2_out), .in1(Funct), .out(multiplexer_3_out), .sel(ALUOp[1]));
  Multiplexer #(.select(2), .width(8)) multiplexer_4 (
    .in0(and_4_out), .in1(or_2_out), .in2(adder_2_out), .in3(adder_2_out), .out(ALUSaida),
    .sel(multiplexer_3_out));
  xnor xnor_1 (xnor_1_out, B[0], A[0]);
  xnor xnor_2 (xnor_2_out, B[1], A[1]);
  xnor xnor_3 (xnor_3_out, B[2], A[2]);
  xnor xnor_4 (xnor_4_out, B[3], A[3]);
  xnor xnor_5 (xnor_5_out, B[4], A[4]);
  xnor xnor_6 (xnor_6_out, B[5], A[5]);
  xnor xnor_7 (xnor_7_out, B[6], A[6]);
  xnor xnor_8 (xnor_8_out, B[7], A[7]);
  and and_5 (ZERO, xnor_1_out, xnor_2_out, xnor_3_out, xnor_4_out, xnor_5_out, xnor_6_out, xnor_7_out, xnor_8_out);
endmodule
