// Logisim project Banco_registradores.circ as structural Verilog: 1 circuit, main circuit Banco_registradores
module Banco_registradores (
  input  [7:0] Data_Write,
  input  [1:0] RS_reg,
  input  [1:0] RD_Reg,
  input  [1:0] RT_reg,
  input  RegWrite,
  input  CLOCK,
  input  RESET,
  output [7:0] R0,
  output [7:0] R1,
  output [7:0] R2,
  output [7:0] R3,
  output [7:0] RS,
  output [7:0] RT
);

  wire and_1_out, and_2_out, and_3_out, and_4_out, decoder_1_out0, decoder_1_out1, decoder_1_out2,
       decoder_1_out3, or_1_out, or_2_out, or_3_out, or_4_out;
  wire [7:0] multiplexer_1_out, multiplexer_2_out, multiplexer_3_out, multiplexer_4_out;

  Decoder #(.select(2)) decoder_1 (
    .out0(decoder_1_out0), .out1(decoder_1_out1), .out2(decoder_1_out2), .out3(decoder_1_out3), .sel(RD_Reg));  // open: en
  and and_1 (and_1_out, decoder_1_out0, RegWrite);
  and and_2 (and_2_out, decoder_1_out1, RegWrite);
  and and_3 (and_3_out, decoder_1_out2, RegWrite);
  and and_4 (and_4_out, decoder_1_out3, RegWrite);
  or or_1 (or_1_out, and_2_out, RESET);
  or or_2 (or_2_out, and_3_out, RESET);
  or or_3 (or_3_out, and_4_out, RESET);
  or or_4 (or_4_out, and_1_out, RESET);
  Multiplexer #(.width(8)) multiplexer_1 (.in0(Data_Write), .in1({8{1'b0}}), .out(multiplexer_1_out), .sel(RESET));
  Multiplexer #(.width(8)) multiplexer_2 (.in0(Data_Write), .in1(8'h2d), .out(multiplexer_2_out), .sel(RESET));
  Multiplexer #(.width(8)) multiplexer_3 (.in0(Data_Write), .in1(8'h83), .out(multiplexer_3_out), .sel(RESET));
  Multiplexer #(.width(8)) multiplexer_4 (.in0(Data_Write), .in1(8'h2d), .out(multiplexer_4_out), .sel(RESET));
  Register register_1 (.D(multiplexer_1_out), .en(or_4_out), .clk(CLOCK), .Q(R0));  // open: clr
  Register register_2 (.D(multiplexer_2_out), .en(or_1_out), .clk(CLOCK), .Q(R1));  // open: clr
  Register register_3 (.D(multiplexer_3_out), .en(or_2_out), .clk(CLOCK), .Q(R2));  // open: clr
  Register register_4 (.D(multiplexer_4_out), .en(or_3_out), .clk(CLOCK), .Q(R3));  // open: clr
  Multiplexer #(.select(2), .width(8)) multiplexer_5 (.in0(R0), .in1(R1), .in2(R2), .in3(R3), .out(RS), .sel(RS_reg));
  Multiplexer #(.select(2), .width(8)) multiplexer_6 (.in0(R0), .in1(R1), .in2(R2), .in3(R3), .out(RT), .sel(RT_reg));
endmodule
