// Logisim project IR.circ as structural Verilog: 1 circuit, main circuit IR
module IR (
  input  [7:0] Entrada,
  input  IRWrite,
  input  CLOCK,
  input  RESET,
  output [1:0] RS,
  output [1:0] RT,
  output [1:0] RD,
  output OpCode,
  output [1:0] Funct,
  output [3:0] IMM
);

  wire or_1_out;

  Register register_1 (.D(Entrada), .en(IRWrite), .clk(CLOCK), .Q({RS, RT, IMM[3:2], Funct}), .clr(RESET));
  or or_1 (or_1_out, IMM[2], IMM[3]);
  not not_1 (OpCode, or_1_out);

  assign IMM[1:0] = Funct;
  assign RD = IMM[3:2];
endmodule
