// Logisim project parte1_cache.circ as structural Verilog: 5 circuits, main circuit main
module main (
  input  [7:0] ENDERECO,
  input  [7:0] DESLOCAMENTO,
  input  [7:0] DADO_IN,
  input  RESET,
  output A5,
  output A4,
  output A3,
  output A2,
  output A1,
  output A0,
  output IGUAIS,
  output out_12
);

  wire bits_validade_1_valido_linha, CLK_out, detetor_primo_1_primo, not_1_out, not_3_out, or_1_out,
       xor_sintetizado_1_s, xor_sintetizado_2_s, xor_sintetizado_3_s;
  wire [2:0] rotulos_1_rotulo_save;
  wire [3:0] bcd_to_7_segment_decoder_1_p1;
  wire [7:6] adder_1_out;

  LED DESLOCAMENTO_LED (.in(A0));
  Adder adder_1 (
    .a(ENDERECO), .b(DESLOCAMENTO), .out({adder_1_out, A5, A4, A3, A2, A1, A0}), .cin(1'b0));  // open: cout
  Clock CLK (.out(CLK_out));
  LED miss (.in(not_1_out));
  not not_1 (not_1_out, out_12);
  detetor_primo detetor_primo_1 (.V0(A3), .V1(A4), .V2(A5), .V3(1'b0), .PRIMO(detetor_primo_1_primo));
  rotulos rotulos_1 (
    .CLK(RESET), .MISS(not_1_out), .A1(A1), .A2(A2), .ROTULO({A5, A4, A3}),
    .ROTULO_SAVE(rotulos_1_rotulo_save));
  bits_validade bits_validade_1 (
    .A2(A2), .A1(A1), .MISS(not_1_out), .CLK(CLK_out), .RESET(RESET),
    .VALIDO_LINHA(bits_validade_1_valido_linha));
  LED led_1 (.in(detetor_primo_1_primo));
  LED VALIDO (.in(bits_validade_1_valido_linha));
  xor_sintetizado xor_sintetizado_1 (.A(A3), .B(rotulos_1_rotulo_save[0]), .S(xor_sintetizado_1_s));
  xor_sintetizado xor_sintetizado_2 (.A(A4), .B(rotulos_1_rotulo_save[1]), .S(xor_sintetizado_2_s));
  xor_sintetizado xor_sintetizado_3 (.A(A5), .B(rotulos_1_rotulo_save[2]), .S(xor_sintetizado_3_s));
  LED led_2 (.in(IGUAIS));
  or or_1 (or_1_out, xor_sintetizado_1_s, xor_sintetizado_2_s, xor_sintetizado_3_s);
  not not_2 (IGUAIS, or_1_out);
  LED hit (.in(out_12));
  and and_1 (out_12, IGUAIS, bits_validade_1_valido_linha);
  // BCD_to_7_Segment_decoder bcd_to_7_segment_decoder_1: pin names not known; wires that end beside it: bcd_to_7_segment_decoder_1_p1
  _7_Segment_Display u_7_segment_display_1 ();  // open: g, f, a, b, e, d, c, dp
  Counter #(.max('hf), .width(4)) counter_1 (
    .count(out_12), .Q(bcd_to_7_segment_decoder_1_p1), .clk(CLK_out), .clr(RESET));  // open: load, D, carry, up
  not not_3 (not_3_out, CLK_out);
  RAM #(.addrWidth(3)) ram_1 (
    .addr({A2, A1, A0}), .we(out_12), .oe(1'b1), .clk(not_3_out), .din(DADO_IN));  // open: dout

  // Notes on the sheet:
  //   A5-A4-A3-A2-A1-A0
  //   Se 1, offset é ativado
  //   S0-S1-S2
  //   É_PRIMO
  //   T0-T1-T2
  //   PORTA XOR SINTETIZADAS T0,T1,T2 - S0,S1,S2
  //   ACERTO
endmodule

module xor_sintetizado (
  input  A,
  input  B,
  output S
);

  wire and_1_out, and_2_out, not_1_out, not_2_out;

  not not_1 (not_1_out, B);
  not not_2 (not_2_out, A);
  and and_1 (and_1_out, A, not_1_out);
  and and_2 (and_2_out, B, not_2_out);
  or or_1 (S, and_1_out, and_2_out);
endmodule

module detetor_primo (
  input  V0,
  input  V1,
  input  V2,
  input  V3,
  output PRIMO
);

  wire and_1_out, and_2_out, and_3_out, and_4_out, not_1_out, not_2_out, not_3_out;

  not not_1 (not_1_out, V1);
  not not_2 (not_2_out, V2);
  not not_3 (not_3_out, V3);
  and and_1 (and_1_out, not_3_out, not_2_out, V1);
  and and_2 (and_2_out, not_3_out, V1, V0);
  and and_3 (and_3_out, not_1_out, V2, V0);
  and and_4 (and_4_out, not_2_out, V1, V0);
  or or_1 (PRIMO, and_1_out, and_2_out, and_3_out, and_4_out);
endmodule

module bits_validade (
  input  A2,
  input  A1,
  input  MISS,
  input  CLK,
  input  RESET,
  output VALIDO_LINHA
);

  wire d_ff_1_q, d_ff_2_q, d_ff_3_q, d_ff_4_q, decoder_1_out0, decoder_1_out1, decoder_1_out2,
       decoder_1_out3, or_1_out, or_2_out, or_3_out, or_4_out;

  Decoder #(.select(2)) decoder_1 (
    .out0(decoder_1_out0), .out1(decoder_1_out1), .out2(decoder_1_out2), .out3(decoder_1_out3),
    .sel({A1, A2}), .en(MISS));
  or or_1 (or_1_out, d_ff_1_q, decoder_1_out0);
  or or_2 (or_2_out, d_ff_2_q, decoder_1_out1);
  or or_3 (or_3_out, d_ff_3_q, decoder_1_out2);
  or or_4 (or_4_out, d_ff_4_q, decoder_1_out3);
  D_Flip_Flop d_ff_1 (.D(or_1_out), .clk(CLK), .Q(d_ff_1_q), .reset(RESET));  // open: Qn, preset
  D_Flip_Flop d_ff_2 (.D(or_2_out), .clk(CLK), .Q(d_ff_2_q), .reset(RESET));  // open: Qn, preset
  D_Flip_Flop d_ff_3 (.D(or_3_out), .clk(CLK), .Q(d_ff_3_q), .reset(RESET));  // open: Qn, preset
  D_Flip_Flop d_ff_4 (.D(or_4_out), .clk(CLK), .Q(d_ff_4_q), .reset(RESET));  // open: Qn, preset
  Multiplexer #(.select(2)) multiplexer_1 (
    .in0(d_ff_1_q), .in1(d_ff_2_q), .in2(d_ff_3_q), .in3(d_ff_4_q), .out(VALIDO_LINHA), .sel({A1, A2}));
endmodule

module rotulos (
  input  CLK,
  input  MISS,
  input  A1,
  input  A2,
  input  [2:0] ROTULO,
  output [2:0] ROTULO_SAVE
);

  wire decoder_1_out0, decoder_1_out1, decoder_1_out2, decoder_1_out3;
  wire [2:0] register_1_q, register_2_q, register_3_q, register_4_q;

  Decoder #(.select(2)) decoder_1 (
    .out0(decoder_1_out0), .out1(decoder_1_out1), .out2(decoder_1_out2), .out3(decoder_1_out3),
    .sel({A2, A1}), .en(MISS));
  Register #(.width(3)) register_1 (.D(ROTULO), .en(decoder_1_out0), .clk(CLK), .Q(register_1_q));  // open: clr
  Register #(.width(3)) register_2 (.D(ROTULO), .en(decoder_1_out1), .clk(CLK), .Q(register_2_q));  // open: clr
  Register #(.width(3)) register_3 (.D(ROTULO), .en(decoder_1_out2), .clk(CLK), .Q(register_3_q));  // open: clr
  Register #(.width(3)) register_4 (.D(ROTULO), .en(decoder_1_out3), .clk(CLK), .Q(register_4_q));  // open: clr
  Multiplexer #(.select(2), .width(3)) multiplexer_1 (
    .in0(register_1_q), .in1(register_2_q), .in2(register_3_q), .in3(register_4_q), .out(ROTULO_SAVE),
    .sel({A2, A1}));
endmodule
