// Logisim project parte1_memoria.circ as structural Verilog: 4 circuits, main circuit main
module main (
  input  [5:0] ENDERECO,
  input  WE,
  input  CLK,
  input  [7:0] DADO_IN,
  output [7:0] DADO_OUT,
  output ERRO_PARIDADE
);

  wire and_1_out, and_2_out, and_3_out, decoder_1_out0, decoder_1_out1, decoder_1_out2, decoder_1_out3,
       PARIDADE_ESCRITA_out, PARIDADE_LEITURA_out, RAM_PARIDADE_dout, xor_sintetizado_1_s;
  wire [7:0] BANCO_REGISTRADORES_dout, MEMORIA_RAM_dout, MEMORIA_ROM_data, REGIAO_ES_dout;

  Decoder #(.enable("false"), .select(2)) decoder_1 (
    .out0(decoder_1_out0), .out1(decoder_1_out1), .out2(decoder_1_out2), .out3(decoder_1_out3),
    .sel(ENDERECO[5:4]));
  LED CS_ROM_ATIVO (.in(decoder_1_out0));
  LED CS_RAM_ATIVO (.in(decoder_1_out1));
  LED CS_REG_ATIVO (.in(decoder_1_out2));
  LED CS_IO_ATIVO (.in(decoder_1_out3));
  and and_1 (and_1_out, WE, decoder_1_out1);
  and and_2 (and_2_out, decoder_1_out2, WE);
  and and_3 (and_3_out, WE, decoder_1_out3);
  ROM #(.addrWidth(4)) MEMORIA_ROM (.addr(ENDERECO[3:0]), .data(MEMORIA_ROM_data));
  RAM #(.addrWidth(4)) MEMORIA_RAM (
    .addr(ENDERECO[3:0]), .we(and_1_out), .clk(CLK), .din(DADO_IN), .dout(MEMORIA_RAM_dout));  // open: oe
  RAM #(.addrWidth(4)) BANCO_REGISTRADORES (
    .addr(ENDERECO[3:0]), .we(and_2_out), .clk(CLK), .din(DADO_IN), .dout(BANCO_REGISTRADORES_dout));  // open: oe
  RAM #(.addrWidth(4)) REGIAO_ES (
    .addr(ENDERECO[3:0]), .we(and_3_out), .clk(CLK), .din(DADO_IN), .dout(REGIAO_ES_dout));  // open: oe
  xor PARIDADE_ESCRITA (PARIDADE_ESCRITA_out, DADO_IN[0], DADO_IN[1], DADO_IN[2], DADO_IN[3], DADO_IN[4], DADO_IN[5], DADO_IN[6], DADO_IN[7]);
  RAM #(.addrWidth(4), .dataWidth(1)) RAM_PARIDADE (
    .addr(ENDERECO[3:0]), .we(and_1_out), .clk(CLK), .din(PARIDADE_ESCRITA_out), .dout(RAM_PARIDADE_dout));  // open: oe
  xor PARIDADE_LEITURA (PARIDADE_LEITURA_out, MEMORIA_RAM_dout[0], MEMORIA_RAM_dout[1], MEMORIA_RAM_dout[2], MEMORIA_RAM_dout[3], MEMORIA_RAM_dout[4], MEMORIA_RAM_dout[5], MEMORIA_RAM_dout[6], MEMORIA_RAM_dout[7]);
  Multiplexer #(.select(2), .width(8)) multiplexer_1 (
    .in0(MEMORIA_ROM_data), .in1(MEMORIA_RAM_dout), .in2(BANCO_REGISTRADORES_dout), .in3(REGIAO_ES_dout),
    .out(DADO_OUT), .sel(ENDERECO[5:4]));
  xor_sintetizado xor_sintetizado_1 (.A(PARIDADE_LEITURA_out), .B(RAM_PARIDADE_dout), .S(xor_sintetizado_1_s));
  and and_4 (ERRO_PARIDADE, decoder_1_out1, xor_sintetizado_1_s);
  LED LED_ERRO_PARIDADE (.in(ERRO_PARIDADE));

  // Notes on the sheet:
  //   contents of MEMORIA_ROM (hex, n*v repeats v):
  //   1
endmodule

module parte1_memoria (
  input  [5:0] ENDERECO,
  input  WE,
  input  CLK,
  input  [7:0] DADO_IN,
  output [7:0] DADO_OUT,
  output ERRO_PARIDADE
);

  wire and_1_out, and_2_out, and_3_out, decoder_1_out0, decoder_1_out1, decoder_1_out2, decoder_1_out3,
       PARIDADE_ESCRITA_out, PARIDADE_LEITURA_out, RAM_PARIDADE_dout, xor_1_out;
  wire [7:0] BANCO_REGISTRADORES_dout, MEMORIA_RAM_dout, MEMORIA_ROM_data, REGIAO_ES_dout;

  Decoder #(.enable("false"), .select(2)) decoder_1 (
    .out0(decoder_1_out0), .out1(decoder_1_out1), .out2(decoder_1_out2), .out3(decoder_1_out3),
    .sel(ENDERECO[5:4]));
  LED CS_ROM_ATIVO (.in(decoder_1_out0));
  LED CS_RAM_ATIVO (.in(decoder_1_out1));
  LED CS_REG_ATIVO (.in(decoder_1_out2));
  LED CS_IO_ATIVO (.in(decoder_1_out3));
  and and_1 (and_1_out, WE, decoder_1_out1);
  and and_2 (and_2_out, decoder_1_out2, WE);
  and and_3 (and_3_out, WE, decoder_1_out3);
  ROM #(.addrWidth(4)) MEMORIA_ROM (.addr(ENDERECO[3:0]), .data(MEMORIA_ROM_data));
  RAM #(.addrWidth(4)) MEMORIA_RAM (
    .addr(ENDERECO[3:0]), .we(and_1_out), .clk(CLK), .din(DADO_IN), .dout(MEMORIA_RAM_dout));  // open: oe
  RAM #(.addrWidth(4)) BANCO_REGISTRADORES (
    .addr(ENDERECO[3:0]), .we(and_2_out), .clk(CLK), .din(DADO_IN), .dout(BANCO_REGISTRADORES_dout));  // open: oe
  RAM #(.addrWidth(4)) REGIAO_ES (
    .addr(ENDERECO[3:0]), .we(and_3_out), .clk(CLK), .din(DADO_IN), .dout(REGIAO_ES_dout));  // open: oe
  xor PARIDADE_ESCRITA (PARIDADE_ESCRITA_out, DADO_IN[0], DADO_IN[1], DADO_IN[2], DADO_IN[3], DADO_IN[5], DADO_IN[6], DADO_IN[7]);
  RAM #(.addrWidth(4), .dataWidth(1)) RAM_PARIDADE (
    .addr(ENDERECO[3:0]), .we(and_1_out), .clk(CLK), .din(PARIDADE_ESCRITA_out), .dout(RAM_PARIDADE_dout));  // open: oe
  xor PARIDADE_LEITURA (PARIDADE_LEITURA_out, MEMORIA_RAM_dout[0], MEMORIA_RAM_dout[1], MEMORIA_RAM_dout[2], MEMORIA_RAM_dout[3], MEMORIA_RAM_dout[5], MEMORIA_RAM_dout[6], MEMORIA_RAM_dout[7]);
  Multiplexer #(.select(2), .width(8)) multiplexer_1 (
    .in0(MEMORIA_ROM_data), .in1(MEMORIA_RAM_dout), .in2(BANCO_REGISTRADORES_dout), .in3(REGIAO_ES_dout),
    .out(DADO_OUT), .sel(ENDERECO[5:4]));
  xor xor_1 (xor_1_out, RAM_PARIDADE_dout, PARIDADE_LEITURA_out);
  and and_4 (ERRO_PARIDADE, decoder_1_out1, xor_1_out);
  LED LED_ERRO_PARIDADE (.in(ERRO_PARIDADE));

  // Notes on the sheet:
  //   contents of MEMORIA_ROM (hex, n*v repeats v):
  //   1
endmodule

module otras_cosas (
  input  CS_ROM,
  input  CS_RAM,
  input  CS_REG,
  input  CS_IO
);

  wire and_1_out, and_2_out, and_3_out, and_4_out, and_5_out, and_6_out, not_1_out, not_2_out, not_3_out,
       not_4_out, not_5_out, not_6_out, undriven, undriven_2;

  // NOT_Gate not_1 has open pins: in=open, out=not_1_out
  // NOT_Gate not_2 has open pins: in=open, out=not_2_out
  // NOT_Gate not_3 has open pins: in=open, out=not_3_out
  // NOT_Gate not_4 has open pins: in=open, out=not_4_out
  // NOT_Gate not_5 has open pins: in=open, out=not_5_out
  // NOT_Gate not_6 has open pins: in=open, out=not_6_out
  and and_1 (and_1_out, not_1_out, undriven);
  and and_2 (and_2_out, not_2_out, undriven_2);
  buf and_3 (and_3_out, not_3_out);  // AND_Gate
  buf and_4 (and_4_out, not_4_out);  // AND_Gate
  buf and_5 (and_5_out, not_5_out);  // AND_Gate
  buf and_6 (and_6_out, not_6_out);  // AND_Gate
  // OR_Gate or_1 has open pins: in0=and_1_out, in1=and_2_out, in2=and_3_out, in3=and_4_out, in4=and_5_out, in5=and_6_out, out=open
endmodule

module xor_sintetizado (
  input  A,
  input  B,
  output S
);

  wire and_1_out, and_2_out, not_1_out, not_2_out;

  not not_1 (not_1_out, B);
  not not_2 (not_2_out, A);
  and and_1 (and_1_out, A, not_1_out);
  and and_2 (and_2_out, B, not_2_out);
  or or_1 (S, and_1_out, and_2_out);
endmodule
