// Logisim project parte2_cabeada.circ as structural Verilog: 5 circuits, main circuit main
module main (
  input  RESET_global,
  output [7:0] out_2,
  output [7:0] out_3,
  output [7:0] out_4,
  output [7:0] out_5,
  output [1:0] out_6,
  output [1:0] ALUOp,
  output [1:0] out_8
);

  wire and_1_out, and_2_out, Clock_global_out, ir_1_opcode, or_1_out, uc_cabeada_1_alusourcea,
       uc_cabeada_1_irwrite, uc_cabeada_1_memread, uc_cabeada_1_pcsource, uc_cabeada_1_pcwrite,
       uc_cabeada_1_pcwritecond, uc_cabeada_1_regwrite, ULA_zero;
  wire [1:0] ir_1_rd, ir_1_rs, ir_1_rt;
  wire [3:0] ir_1_imm;
  wire [7:0] A_q, ALUOut_q, B_q, bit_extender_1_out, multiplexer_1_out, multiplexer_2_out, multiplexer_3_out,
       multiplexer_4_out, PC_q, Register_bank_rs, Register_bank_rt, ROM_Prog_data, shifter_1_out,
       ULA_alusaida;

  Clock Clock_global (.out(Clock_global_out));
  Register PC (.D(multiplexer_4_out), .en(or_1_out), .clk(Clock_global_out), .Q(PC_q), .clr(RESET_global));
  and and_1 (and_1_out, ~RESET_global, Clock_global_out);  // AND_Gate
  ROM ROM_Prog (.addr(PC_q), .data(ROM_Prog_data));
  or or_1 (or_1_out, uc_cabeada_1_pcwrite, and_2_out);
  UC_cabeada uc_cabeada_1 (
    .CLOCK(and_1_out), .OpCode(ir_1_opcode), .PCWrite(uc_cabeada_1_pcwrite),
    .PCWriteCond(uc_cabeada_1_pcwritecond), .PCSource(uc_cabeada_1_pcsource), .MemRead(uc_cabeada_1_memread),
    .IRWRite(uc_cabeada_1_irwrite), .RegWrite(uc_cabeada_1_regwrite), .ALUSourceA(uc_cabeada_1_alusourcea),
    .ALUSourceB(out_8), .ALUOp(ALUOp));
  Multiplexer #(.width(8)) multiplexer_1 (
    .in0({8{1'b0}}), .in1(ROM_Prog_data), .out(multiplexer_1_out), .sel(uc_cabeada_1_memread));
  and and_2 (and_2_out, uc_cabeada_1_pcwritecond, ULA_zero);
  IR ir_1 (
    .Entrada(multiplexer_1_out), .CLOCK(Clock_global_out), .IRWrite(uc_cabeada_1_irwrite),
    .RESET(RESET_global), .IMM(ir_1_imm), .RS(ir_1_rs), .RT(ir_1_rt), .RD(ir_1_rd), .Funct(out_6),
    .OpCode(ir_1_opcode));
  assign bit_extender_1_out = {{4{ir_1_imm[3]}}, ir_1_imm};  // Bit_Extender bit_extender_1
  Banco_registradores Register_bank (
    .RS_reg(ir_1_rs), .RT_reg(ir_1_rt), .RD_Reg(ir_1_rd), .RegWrite(uc_cabeada_1_regwrite),
    .Data_Write(ALUOut_q), .CLOCK(Clock_global_out), .RESET(RESET_global), .R0(out_2), .R1(out_3),
    .R2(out_4), .R3(out_5), .RS(Register_bank_rs), .RT(Register_bank_rt));
  Register A (.D(Register_bank_rs), .en(1'b1), .clk(Clock_global_out), .Q(A_q), .clr(RESET_global));
  Register B (.D(Register_bank_rt), .en(1'b1), .clk(Clock_global_out), .Q(B_q), .clr(RESET_global));
  Shifter shifter_1 (.in(bit_extender_1_out), .\dist (3'b010), .out(shifter_1_out));
  Multiplexer #(.select(2), .width(8)) multiplexer_2 (
    .in0(B_q), .in1(8'h1), .in2(shifter_1_out), .in3({8{1'b0}}), .out(multiplexer_2_out), .sel(out_8));
  Multiplexer #(.width(8)) multiplexer_3 (
    .in0(PC_q), .in1(A_q), .out(multiplexer_3_out), .sel(uc_cabeada_1_alusourcea));
  ALU ULA (
    .A(multiplexer_3_out), .B(multiplexer_2_out), .ALUOp(ALUOp), .Funct(out_6), .ZERO(ULA_zero),
    .ALUSaida(ULA_alusaida));  // open: Overflow
  Register ALUOut (.D(ULA_alusaida), .en(1'b1), .clk(Clock_global_out), .Q(ALUOut_q), .clr(RESET_global));
  Multiplexer #(.width(8)) multiplexer_4 (
    .in0(ULA_alusaida), .in1(ALUOut_q), .out(multiplexer_4_out), .sel(uc_cabeada_1_pcsource));

  // Notes on the sheet:
  //   contents of ROM_Prog (hex, n*v repeats v):
  //   73 12*0 63
  //   LerMem
  //   PCWrite
  //   IRWrite
  //   PCWriteCond
  //   Zero da ULA
  //   RegWrite
  //   ALUSourceB
  //   ALUSourceA
  //   PCSource
endmodule

module ALU (
  input  [7:0] A,
  input  [7:0] B,
  input  [1:0] Funct,
  input  [1:0] ALUOp,
  output ZERO,
  output [7:0] ALUSaida,
  output Overflow
);

  wire and_1_out, and_2_out, and_3_out, or_1_out, xnor_1_out, xnor_2_out, xnor_3_out, xnor_4_out, xnor_5_out,
       xnor_6_out, xnor_7_out, xnor_8_out;
  wire [1:0] multiplexer_2_out, multiplexer_3_out;
  wire [7:0] adder_1_out, adder_2_out, and_4_out, multiplexer_1_out, not_1_out, or_2_out;

  assign not_1_out = ~B;  // NOT_Gate not_1, 8 bits wide
  Multiplexer #(.width(8)) multiplexer_1 (.in0(B), .in1(adder_1_out), .out(multiplexer_1_out), .sel(or_1_out));
  Adder adder_1 (.a(not_1_out), .b(8'h1), .out(adder_1_out));  // open: cin, cout
  or or_1 (or_1_out, and_1_out, and_2_out);
  and and_1 (and_1_out, Funct[0], Funct[1], ALUOp[1]);
  and and_2 (and_2_out, ~ALUOp[1], ALUOp[0]);  // AND_Gate
  Adder adder_2 (.a(A), .b(multiplexer_1_out), .out(adder_2_out), .cout(Overflow));  // open: cin
  Multiplexer #(.width(2)) multiplexer_2 (.in0(2'b10), .in1(2'b11), .out(multiplexer_2_out), .sel(and_3_out));
  and and_3 (and_3_out, ~ALUOp[0], ~ALUOp[1]);  // AND_Gate
  assign and_4_out = A & multiplexer_1_out;  // AND_Gate and_4, 8 bits wide
  assign or_2_out = A | multiplexer_1_out;  // OR_Gate or_2, 8 bits wide
  Multiplexer #(.width(2)) multiplexer_3 (
    .in0(multiplexer_2_out), .in1(Funct), .out(multiplexer_3_out), .sel(ALUOp[1]));
  Multiplexer #(.select(2), .width(8)) multiplexer_4 (
    .in0(and_4_out), .in1(or_2_out), .in2(adder_2_out), .in3(adder_2_out), .out(ALUSaida),
    .sel(multiplexer_3_out));
  xnor xnor_1 (xnor_1_out, B[0], A[0]);
  xnor xnor_2 (xnor_2_out, B[1], A[1]);
  xnor xnor_3 (xnor_3_out, B[2], A[2]);
  xnor xnor_4 (xnor_4_out, B[3], A[3]);
  xnor xnor_5 (xnor_5_out, B[4], A[4]);
  xnor xnor_6 (xnor_6_out, B[5], A[5]);
  xnor xnor_7 (xnor_7_out, B[6], A[6]);
  xnor xnor_8 (xnor_8_out, B[7], A[7]);
  and and_5 (ZERO, xnor_1_out, xnor_2_out, xnor_3_out, xnor_4_out, xnor_5_out, xnor_6_out, xnor_7_out, xnor_8_out);
endmodule

module Banco_registradores (
  input  [7:0] Data_Write,
  input  [1:0] RS_reg,
  input  [1:0] RD_Reg,
  input  [1:0] RT_reg,
  input  RegWrite,
  input  CLOCK,
  input  RESET,
  output [7:0] R0,
  output [7:0] R1,
  output [7:0] R2,
  output [7:0] R3,
  output [7:0] RS,
  output [7:0] RT
);

  wire and_1_out, and_2_out, and_3_out, and_4_out, decoder_1_out0, decoder_1_out1, decoder_1_out2,
       decoder_1_out3, or_1_out, or_2_out, or_3_out, or_4_out;
  wire [7:0] multiplexer_1_out, multiplexer_2_out, multiplexer_3_out, multiplexer_4_out;

  Decoder #(.select(2)) decoder_1 (
    .out0(decoder_1_out0), .out1(decoder_1_out1), .out2(decoder_1_out2), .out3(decoder_1_out3), .sel(RD_Reg));  // open: en
  and and_1 (and_1_out, decoder_1_out0, RegWrite);
  and and_2 (and_2_out, decoder_1_out1, RegWrite);
  and and_3 (and_3_out, decoder_1_out2, RegWrite);
  and and_4 (and_4_out, decoder_1_out3, RegWrite);
  or or_1 (or_1_out, and_2_out, RESET);
  or or_2 (or_2_out, and_3_out, RESET);
  or or_3 (or_3_out, and_4_out, RESET);
  or or_4 (or_4_out, and_1_out, RESET);
  Multiplexer #(.width(8)) multiplexer_1 (.in0(Data_Write), .in1({8{1'b0}}), .out(multiplexer_1_out), .sel(RESET));
  Multiplexer #(.width(8)) multiplexer_2 (.in0(Data_Write), .in1(8'h2d), .out(multiplexer_2_out), .sel(RESET));
  Multiplexer #(.width(8)) multiplexer_3 (.in0(Data_Write), .in1(8'h83), .out(multiplexer_3_out), .sel(RESET));
  Multiplexer #(.width(8)) multiplexer_4 (.in0(Data_Write), .in1(8'h2d), .out(multiplexer_4_out), .sel(RESET));
  Register register_1 (.D(multiplexer_1_out), .en(or_4_out), .clk(CLOCK), .Q(R0));  // open: clr
  Register register_2 (.D(multiplexer_2_out), .en(or_1_out), .clk(CLOCK), .Q(R1));  // open: clr
  Register register_3 (.D(multiplexer_3_out), .en(or_2_out), .clk(CLOCK), .Q(R2));  // open: clr
  Register register_4 (.D(multiplexer_4_out), .en(or_3_out), .clk(CLOCK), .Q(R3));  // open: clr
  Multiplexer #(.select(2), .width(8)) multiplexer_5 (.in0(R0), .in1(R1), .in2(R2), .in3(R3), .out(RS), .sel(RS_reg));
  Multiplexer #(.select(2), .width(8)) multiplexer_6 (.in0(R0), .in1(R1), .in2(R2), .in3(R3), .out(RT), .sel(RT_reg));
endmodule

module IR (
  input  [7:0] Entrada,
  input  IRWrite,
  input  CLOCK,
  input  RESET,
  output [1:0] RS,
  output [1:0] RT,
  output [1:0] RD,
  output OpCode,
  output [1:0] Funct,
  output [3:0] IMM
);

  wire or_1_out;

  Register register_1 (.D(Entrada), .en(IRWrite), .clk(CLOCK), .Q({RS, RT, IMM[3:2], Funct}), .clr(RESET));
  or or_1 (or_1_out, IMM[2], IMM[3]);
  not not_1 (OpCode, or_1_out);

  assign IMM[1:0] = Funct;
  assign RD = IMM[3:2];
endmodule

module UC_cabeada (
  input  CLOCK,
  input  OpCode,
  output PCWrite,
  output PCWriteCond,
  output PCSource,
  output MemRead,
  output IRWRite,
  output RegWrite,
  output ALUSourceA,
  output [1:0] ALUSourceB,
  output [1:0] ALUOp
);

  wire and_1_out, and_2_out, and_3_out, and_4_out, and_5_out, and_6_out, and_8_out, and_9_out, d_ff_1_q,
       d_ff_1_qn, d_ff_2_q, d_ff_3_q, or_1_out, or_2_out, or_3_out, or_4_out, or_5_out, or_6_out, or_7_out,
       or_8_out, or_9_out, or_10_out;
  wire [1:0] and_12_out, and_13_out, and_14_out, and_15_out, bit_extender_1_out, bit_extender_2_out,
       bit_extender_3_out, bit_extender_4_out;

  D_Flip_Flop d_ff_1 (.D(d_ff_1_qn), .clk(CLOCK), .Q(d_ff_1_q), .Qn(d_ff_1_qn), .reset(or_2_out));  // open: preset
  and and_1 (and_1_out, d_ff_2_q, ~d_ff_1_q);  // AND_Gate
  and and_2 (and_2_out, d_ff_1_q, ~d_ff_2_q);  // AND_Gate
  or or_1 (or_1_out, and_1_out, and_2_out);
  D_Flip_Flop d_ff_2 (.D(and_3_out), .clk(CLOCK), .Q(d_ff_2_q), .reset(or_2_out));  // open: Qn, preset
  and and_3 (and_3_out, or_1_out, ~OpCode);  // AND_Gate
  and and_4 (and_4_out, d_ff_1_q, d_ff_3_q);
  and and_5 (and_5_out, d_ff_2_q, d_ff_3_q);
  or or_2 (or_2_out, and_4_out, and_5_out);
  and and_6 (and_6_out, and_8_out, OpCode);
  or or_3 (or_3_out, d_ff_3_q, and_6_out);
  D_Flip_Flop d_ff_3 (.D(or_3_out), .clk(CLOCK), .Q(d_ff_3_q), .reset(or_2_out));  // open: Qn, preset
  and and_7 (IRWRite, ~d_ff_3_q, ~d_ff_2_q, ~d_ff_1_q);  // AND_Gate
  and and_8 (and_8_out, ~d_ff_3_q, ~d_ff_2_q, d_ff_1_q);  // AND_Gate
  or or_4 (or_4_out, IRWRite, and_8_out, RegWrite, PCSource);
  or or_5 (or_5_out, IRWRite, and_9_out, RegWrite);
  or or_6 (or_6_out, and_9_out, IRWRite);
  and and_9 (and_9_out, ~d_ff_3_q, d_ff_2_q, ~d_ff_1_q);  // AND_Gate
  or or_7 (or_7_out, and_9_out, IRWRite, RegWrite);
  _7_Segment_Display u_7_segment_display_1 (
    .g(or_10_out), .f(or_9_out), .a(or_7_out), .b(or_8_out), .e(or_6_out), .d(or_5_out), .c(or_4_out));  // open: dp
  and and_10 (RegWrite, ~d_ff_3_q, d_ff_2_q, d_ff_1_q);  // AND_Gate
  or or_8 (or_8_out, IRWRite, and_8_out, and_9_out, RegWrite, PCSource);
  or or_9 (or_9_out, IRWRite, PCSource);
  or or_10 (or_10_out, and_9_out, RegWrite, PCSource);
  and and_11 (PCSource, d_ff_3_q, ~d_ff_2_q, ~d_ff_1_q);  // AND_Gate
  assign bit_extender_1_out = {{1{and_9_out}}, and_9_out};  // Bit_Extender bit_extender_1
  or or_11 (ALUSourceA, and_9_out, PCSource);
  assign bit_extender_2_out = {{1{IRWRite}}, IRWRite};  // Bit_Extender bit_extender_2
  assign bit_extender_3_out = {{1{and_8_out}}, and_8_out};  // Bit_Extender bit_extender_3
  assign bit_extender_4_out = {{1{PCSource}}, PCSource};  // Bit_Extender bit_extender_4
  assign and_12_out = bit_extender_2_out & 2'b01;  // AND_Gate and_12, 2 bits wide
  assign ALUSourceB = and_12_out | and_13_out;  // OR_Gate or_12, 2 bits wide
  assign and_13_out = bit_extender_3_out & 2'b10;  // AND_Gate and_13, 2 bits wide
  assign and_14_out = bit_extender_4_out & 2'b01;  // AND_Gate and_14, 2 bits wide
  assign and_15_out = bit_extender_1_out & 2'b10;  // AND_Gate and_15, 2 bits wide
  assign ALUOp = and_14_out | and_15_out;  // OR_Gate or_13, 2 bits wide

  assign MemRead = IRWRite;
  assign PCWrite = IRWRite;
  assign PCWriteCond = PCSource;

  // Notes on the sheet:
  //   Contador
  //   D0 = -Q0
  //   D1 = (Q0 XOR Q1) AND -OP
  //   D2 = (OP AND S1) OR Q2
  //   RESET = Q2 AND (Q0 OR Q1)
  //   Máquina de estados
  //   Q0,Q1,Q2
  //   S0,S1,S2,S3,S4
endmodule
